# Fritzing sketch autosat_v1 (saved by Fritzing 1.0.7)
breadboards: 1

parts:
  A1 = Esp32-c3 super mini
  M1 = gy9250
  Mod1 = TMC2209 [package=THT]
  Module1 = Boladge HMC5883L Compass Module
  U1 = LM2596 step down module
  M2 = Stepper Motor - Bipolar

nets:
  N1: A1.Pin_2, M1.pin4, Module1.SDA
  N2: A1.Pin_3, M1.pin3, Module1.SCL
  N3: A1.Pin_4, Mod1.UART
  N4: A1.Pin_11, Mod1.Step
  N5: A1.Pin_13, Mod1.Dir
  N6: A1.Pin_14, M1.pin1, Mod1.VIO, Mod1.MS1, Mod1.MS2, Module1.VCC
  GND: A1.Pin_15, M1.pin2, Mod1.GND, Mod1.EN, Module1.GND, U1.IN-, U1.OUT-
  N7: A1.Pin_16, U1.OUT+
  N8: Mod1.M1B, M2.A
  N9: Mod1.M1A, M2.C
  N10: Mod1.M2A, M2.B
  N11: Mod1.M2B, M2.D
  N12: Mod1.VM, U1.IN+

custom parts:
  Esp32-c3 super mini: ESP32-C3 Development Board ESP32 SuperMini Development Board ESP32 Development Board WiFi Bluetooth.
  gy9250: MPU-9250 module (three-axis gyroscope + three-axis acceleration + three-axis magnetic field). The generic model from ebay et. al. rather than the Sparkfun version.
  TMC2209: TMC2209-LA stepper motor controller and driver. Supply voltage 4.75-28V Iphase up to 1.77A rms (2.5A peak)
  Boladge HMC5883L Compass Module: Cheap digital compass module
  LM2596 step down module: LM2596 DC-DC step down power supply module 3 A.
